# Fritzing sketch Nuovo_circuito_PlayBot4All (saved by Fritzing 0.9.3b)
stripboards: 1

parts:
  Raspberry_Pi_4 = Raspberry Pi 4 [part_number=RPI-4-b]
  SM7 = 28BYJ-48 Stepper Motor [part_number=28BYJ-48]
  SM8 = 28BYJ-48 Stepper Motor [part_number=28BYJ-48]
  Driver7 = 28BYJ-48 Driver Module [part_number=ULN2003 package=THT]
  Driver8 = 28BYJ-48 Driver Module [part_number=ULN2003 package=THT]
  Mod3 = KY-008 Laser Transmitter Module [package="Breakout board"]
  J5 = Basic Servo
  J6 = Basic Servo
  Power_plug2 = Power plug

nets:
  N1: Raspberry_Pi_4.GPIO2, Raspberry_Pi_4.GPIO3, J5.pulse
  GND: Raspberry_Pi_4.GND, Raspberry_Pi_4.GPIO17, Raspberry_Pi_4.GPIO14, Driver7.GND, Driver8.GND, Mod3.-, J5.gnd, J6.gnd, Power_plug2.GND
  N2: Raspberry_Pi_4.GPIO27, Driver8.IN1
  N3: Raspberry_Pi_4.GPIO22, Raspberry_Pi_4.3V3, Driver8.IN2
  N4: Raspberry_Pi_4.GPIO10, Driver8.IN3
  N5: Raspberry_Pi_4.GPIO9, Raspberry_Pi_4.GPIO11, Driver8.IN4
  N6: Raspberry_Pi_4.GPIO5, Driver7.IN1
  N7: Raspberry_Pi_4.GPIO6, Driver7.IN2
  N8: Raspberry_Pi_4.GPIO13, Driver7.IN3
  N9: Raspberry_Pi_4.GPIO19, Raspberry_Pi_4.GPIO26, Driver7.IN4
  N10: Raspberry_Pi_4.GPIO21, J6.pulse
  N11: Raspberry_Pi_4.ID_SC, Raspberry_Pi_4.GPIO7, Mod3.NC
  VCC: Raspberry_Pi_4.5V, J5.vcc, J6.vcc
  N12: SM7.blue-pin, Driver7.blue-pin
  N13: SM7.pink-pin, Driver7.pink-pin
  N14: SM7.yellow-pin, Driver7.yellow-pin
  N15: SM7.orange-pin, Driver7.orange-pin
  N16: SM7.red-pin, Driver7.red-pin
  N17: SM8.blue-pin, Driver8.blue-pin
  N18: SM8.pink-pin, Driver8.pink-pin
  N19: SM8.yellow-pin, Driver8.yellow-pin
  N20: SM8.orange-pin, Driver8.orange-pin
  N21: SM8.red-pin, Driver8.red-pin
  N22: Driver7.Vmotor, Driver8.Vmotor, Driver8.ON/OFF, Mod3.S, Power_plug2.VCC

notes:
  ASSE Y
  ASSE X

custom parts:
  Raspberry Pi 4: The RPi4, a faster version of the awesome Raspberry Pi 2 B ARM Board with 40 pin gpio. Ready for special Raspberry Pi B+ and RPi2 Hat (Hardware attached (on) top)
  28BYJ-48 Stepper Motor: Unipolar Stepper Motor 28BYJ-48 Top coil - pink & orange Bottom coil - blue & yellow Common rail - red Connector pins: blue - pink - yellow - orange - red
  28BYJ-48 Driver Module: ULN2003 Driver Module for the 28BYJ-48 Unipolar Stepper Motor LED A - Blue wire - Bottom coil left LED B - Pink wire - Top coil left LED C - Yellow wire - Bottom coil right LED D - Orange wire - Top coil right Common rail - red Connector pins: blue - pink - yellow - orange - red Control pins - IN1 to IN4 Power pins - GND & Vmotor (5-12V) On/Off jumper (if removed, power to motor is cut).
  KY-008 Laser Transmitter Module: KY-008 Laser Transmitter Module, emits a dot shaped red laser beam.
